// Digital circuit ControlUnit.dig as structural Verilog
module ControlUnit (
  input  Reset,
  input  [5:0] Opcode,
  output memWrite,
  output memRead,
  output memToReg,
  output [2:0] aluOp,
  output RegDst,
  output aluSrc,
  output RegWrite,
  output branch
);

  wire beq_eq, bne_eq, LW_eq, R_format_eq, SW_eq;
  wire [2:0] priorityencoder_1_num;
  wire [9:0] multiplexer_1_out;

  Comparator #(.Bits(6)) R_format (.a(Opcode), .b({6{1'b0}}), .eq(R_format_eq));  // open: gt, lt
  Comparator #(.Bits(6)) SW (.a(Opcode), .b(6'b101011), .eq(SW_eq));  // open: gt, lt
  Comparator #(.Bits(6)) LW (.a(Opcode), .b(6'b100011), .eq(LW_eq));  // open: gt, lt
  Comparator #(.Bits(6)) beq (.a(Opcode), .b(6'b000100), .eq(beq_eq));  // open: gt, lt
  Comparator #(.Bits(6)) bne (.a(Opcode), .b(6'b000101), .eq(bne_eq));  // open: gt, lt
  PriorityEncoder #(.Selector_Bits(3)) priorityencoder_1 (
    .in0(R_format_eq), .in1(SW_eq), .in2(LW_eq), .in3(beq_eq), .in4(bne_eq), .in5(1'b0), .in6(1'b0),
    .in7(1'b0), .num(priorityencoder_1_num));  // open: any
  Multiplexer #(.Selector_Bits(3), .Bits(10)) multiplexer_1 (
    .sel(priorityencoder_1_num), .in_0(10'h178), .in_1(10'h91), .in_2(10'h196), .in_3(10'h218),
    .in_4(10'h218), .in_5({10{1'b0}}), .in_6({10{1'b0}}), .in_7({10{1'b0}}), .out(multiplexer_1_out));
  Multiplexer #(.Bits(10)) multiplexer_2 (
    .sel(Reset), .in_0(multiplexer_1_out), .in_1({10{1'b0}}),
    .out({branch, RegWrite, aluSrc, RegDst, aluOp, memToReg, memRead, memWrite}));

  // Other names for the same wires on the sheet: rst = Reset
endmodule
