// Digital circuit MIPS32SOC.dig as structural Verilog
module MIPS32SOC (
  input  clk,
  input  Reset
);

  wire alu_1_iszero, aluSrc, and_1_out, branch, jump, memRead, memToReg, memWrite, RegDst, RegWrite;
  wire [2:0] aluFunc, aluOp;
  wire [4:0] multiplexer_2_out;
  wire [5:0] Func, Opcode;
  wire [25:6] Inst_Mem_d;
  wire [27:0] barrelshifter_1_out;
  wire [27:26] undriven;
  wire [31:0] add_1_s, add_2_s, alu_1_res, barrelshifter_2_out, bitextender_1_out, Data_Mem_d,
       multiplexer_1_out, multiplexer_3_out, multiplexer_4_out, multiplexer_5_out, PC_q, Reg_File_da,
       Reg_File_db, wData;

  Multiplexer #(.Bits(32)) multiplexer_1 (
    .sel(Reset), .in_0(multiplexer_5_out), .in_1({32{1'b0}}), .out(multiplexer_1_out));
  Register #(.Bits(32)) PC (.D(multiplexer_1_out), .C(clk), .en(1'b1), .Q(PC_q));
  Add #(.Bits(32)) add_1 (.a(PC_q), .b(32'h4), .c_i(1'b0), .s(add_1_s));  // open: c_o
  ROM #(.AddrBits(8), .Bits(32)) Inst_Mem (.A(PC_q[9:2]), .sel(1'b1), .D({Opcode, Inst_Mem_d, Func}));
  BarrelShifter #(.Bits(28), .barrelSigned("true")) barrelshifter_1 (
    .in({undriven, Inst_Mem_d, Func}), .shift(2'b10), .out(barrelshifter_1_out));
  // ControlUnit controlunit_1: pin names not known; wires that end beside it: Opcode, Reset, aluSrc, RegDst, aluOp, memToReg, memRead, memWrite, RegWrite, branch, jump
  Multiplexer #(.Bits(5)) multiplexer_2 (
    .sel(RegDst), .in_0(Inst_Mem_d[20:16]), .in_1(Inst_Mem_d[15:11]), .out(multiplexer_2_out));
  BitExtender #(.inputBits(16), .outputBits(32)) bitextender_1 (.in({Inst_Mem_d[15:6], Func}), .out(bitextender_1_out));
  RegisterFile #(.AddrBits(5), .Bits(32)) Reg_File (
    .Din(wData), .we(RegWrite), .Rw(multiplexer_2_out), .C(clk), .Ra(Inst_Mem_d[25:21]),
    .Rb(Inst_Mem_d[20:16]), .Da(Reg_File_da), .Db(Reg_File_db));
  BarrelShifter #(.Bits(28), .barrelSigned("true")) barrelshifter_2 (
    .in(bitextender_1_out[27:0]), .shift(2'b10), .out(barrelshifter_2_out[27:0]));
  Multiplexer #(.Bits(32)) multiplexer_3 (
    .sel(aluSrc), .in_0(Reg_File_db), .in_1(bitextender_1_out), .out(multiplexer_3_out));
  Add #(.Bits(32)) add_2 (.a(add_1_s), .b(barrelshifter_2_out), .c_i(1'b0), .s(add_2_s));  // open: c_o
  ALU alu_1 (.a(Reg_File_da), .b(multiplexer_3_out), .op(aluFunc), .res(alu_1_res), .isZero(alu_1_iszero));
  Multiplexer #(.Bits(32)) multiplexer_4 (.sel(and_1_out), .in_0(add_1_s), .in_1(add_2_s), .out(multiplexer_4_out));
  Multiplexer #(.Bits(32)) multiplexer_5 (
    .sel(jump), .in_0({add_1_s[31:28], barrelshifter_1_out}), .in_1(multiplexer_4_out),
    .out(multiplexer_5_out));
  and and_1 (and_1_out, branch, alu_1_iszero);
  ALUControl alucontrol_1 (.aluOp(aluOp), .Func(Func));  // open: aluFunc
  RAMDualPort #(.AddrBits(8), .Bits(32)) Data_Mem (
    .A(alu_1_res[9:2]), .Din(Reg_File_db), .str(memWrite), .C(clk), .ld(memRead), .D(Data_Mem_d));
  Multiplexer #(.Bits(32)) multiplexer_6 (.sel(memToReg), .in_0(alu_1_res), .in_1(Data_Mem_d), .out(wData));
  // Pins of 28 and 32 bits meet at bitextender_1_out
  // Pins of 26 and 28 bits meet at {undriven, Inst_Mem_d, Func}
  // Pins of 28 and 32 bits meet at barrelshifter_2_out

  // Other names for the same wires on the sheet: rst = Reset

  // Notes on the sheet:
  //   contents of Inst_Mem (hex, n*v repeats v):
  //   8c080000,8c090004,ac080008
endmodule
