// Digital circuit ALUControl.dig as structural Verilog
module ALUControl (
  input  [2:0] aluOp,
  input  [5:0] Func,
  output [2:0] aluFunc
);

  wire ADD_eq, ADDI_eq, AND_eq, comparator_1_eq, OR_eq, ORI_eq, priorityencoder_1_any, SLT_eq, SUB_eq, XOR_eq;
  wire [2:0] multiplexer_2_out, priorityencoder_1_num;

  Comparator #(.Bits(6)) AND (.a(Func), .b(6'b100100), .eq(AND_eq));  // open: gt, lt
  Comparator #(.Bits(6)) OR (.a(Func), .b(6'b100101), .eq(OR_eq));  // open: gt, lt
  Comparator #(.Bits(6)) ADD (.a(Func), .b(6'b100000), .eq(ADD_eq));  // open: gt, lt
  Comparator #(.Bits(6)) SUB (.a(Func), .b(6'b100010), .eq(SUB_eq));  // open: gt, lt
  Comparator #(.Bits(6)) SLT (.a(Func), .b(6'b101010), .eq(SLT_eq));  // open: gt, lt
  Comparator #(.Bits(6)) XOR (.a(Func), .b(6'b100110), .eq(XOR_eq));  // open: gt, lt
  Comparator #(.Bits(6)) ADDI (.a(Func), .b(6'b001000), .eq(ADDI_eq));  // open: gt, lt
  Comparator #(.Bits(6)) ORI (.a(Func), .b(6'b001101), .eq(ORI_eq));  // open: gt, lt
  Comparator #(.Bits(3)) comparator_1 (.a(aluOp), .b(3'b111), .eq(comparator_1_eq));  // open: gt, lt
  PriorityEncoder #(.Selector_Bits(3)) priorityencoder_1 (
    .in0(AND_eq), .in1(OR_eq), .in2(ADD_eq), .in3(SUB_eq), .in4(SLT_eq), .in5(XOR_eq), .in6(ADDI_eq),
    .in7(ORI_eq), .num(priorityencoder_1_num), .any(priorityencoder_1_any));
  Multiplexer #(.Bits(3)) multiplexer_1 (.sel(comparator_1_eq), .in_0(aluOp), .in_1(multiplexer_2_out), .out(aluFunc));
  Multiplexer #(.Bits(3)) multiplexer_2 (
    .sel(priorityencoder_1_any), .in_0(3'b101), .in_1(priorityencoder_1_num), .out(multiplexer_2_out));
endmodule
