// Digital circuit ControlUnit.dig as structural Verilog
module ControlUnit (
  input  rst,
  input  [5:0] Opcode,
  output memWrite,
  output memRead,
  output memToReg,
  output [2:0] aluOp,
  output RegDst,
  output aluSrc,
  output RegWrite,
  output beq,
  output jump,
  output bne,
  output zeroExtend
);

  wire addi_eq, andi_eq, beq_eq, bne_eq, jmp_eq, lui_eq, LW_eq, ori_eq, R_format_eq, SW_eq, xori_eq;
  wire [3:0] priorityencoder_1_num;
  wire [12:0] multiplexer_1_out;

  Comparator #(.Bits(6)) R_format (.a(Opcode), .b({6{1'b0}}), .eq(R_format_eq));  // open: gt, lt
  Comparator #(.Bits(6)) SW (.a(Opcode), .b(6'b101011), .eq(SW_eq));  // open: gt, lt
  Comparator #(.Bits(6)) LW (.a(Opcode), .b(6'b100011), .eq(LW_eq));  // open: gt, lt
  Comparator #(.Bits(6)) u_beq (.a(Opcode), .b(6'b000100), .eq(beq_eq));  // open: gt, lt
  Comparator #(.Bits(6)) u_bne (.a(Opcode), .b(6'b000101), .eq(bne_eq));  // open: gt, lt
  Comparator #(.Bits(6)) jmp (.a(Opcode), .b(6'b000010), .eq(jmp_eq));  // open: gt, lt
  Comparator #(.Bits(6)) lui (.a(Opcode), .b(6'b001111), .eq(lui_eq));  // open: gt, lt
  Comparator #(.Bits(6)) addi (.a(Opcode), .b(6'b001000), .eq(addi_eq));  // open: gt, lt
  Comparator #(.Bits(6)) andi (.a(Opcode), .b(6'b001100), .eq(andi_eq));  // open: gt, lt
  Comparator #(.Bits(6)) ori (.a(Opcode), .b(6'b001101), .eq(ori_eq));  // open: gt, lt
  Comparator #(.Bits(6)) xori (.a(Opcode), .b(6'b001110), .eq(xori_eq));  // open: gt, lt
  PriorityEncoder #(.Selector_Bits(4)) priorityencoder_1 (
    .in0(R_format_eq), .in1(SW_eq), .in2(LW_eq), .in3(beq_eq), .in4(bne_eq), .in5(jmp_eq), .in6(lui_eq),
    .in7(addi_eq), .in8(andi_eq), .in9(ori_eq), .in10(xori_eq), .in11(1'b0), .in12(1'b0), .in13(1'b0),
    .in14(1'b0), .in15(1'b0), .num(priorityencoder_1_num));  // open: any
  Multiplexer #(.Selector_Bits(4), .Bits(13)) multiplexer_1 (
    .sel(priorityencoder_1_num), .in_0(13'h178), .in_1(13'h91), .in_2(13'h196), .in_3(13'h218),
    .in_4(13'h418), .in_5(13'h838), .in_6(13'h1b0), .in_7(13'h190), .in_8(13'h1180), .in_9(13'h1188),
    .in_10(13'h11a8), .in_11({13{1'b0}}), .in_12({13{1'b0}}), .in_13({13{1'b0}}), .in_14({13{1'b0}}),
    .in_15({13{1'b0}}), .out(multiplexer_1_out));
  Multiplexer #(.Bits(13)) multiplexer_2 (
    .sel(rst), .in_0(multiplexer_1_out), .in_1({13{1'b0}}),
    .out({zeroExtend, jump, bne, beq, RegWrite, aluSrc, RegDst, aluOp, memToReg, memRead, memWrite}));
endmodule
