// Digital circuit MemDecoder.dig as structural Verilog
module MemDecoder (
  input  [31:0] VirtualAddress,
  input  Enable,
  output [10:0] PhysicalAddress,
  output InvalidAddress
);

  wire and_1_out, and_2_out, and_3_out, GM_2_eq, GM_2_lt, GM_eq, GM_gt, multiplexer_5_out, not_1_out,
       not_2_out, or_1_out, or_2_out, or_3_out, or_4_out, Stack_2_eq, Stack_2_lt, Stack_eq, Stack_gt;
  wire [31:0] add_1_s, multiplexer_1_out, multiplexer_2_out, multiplexer_3_out, multiplexer_4_out;
  wire [31:11] or_5_out;

  Comparator #(.Bits(32)) GM (.a(VirtualAddress), .b(32'h10000000), .gt(GM_gt), .eq(GM_eq));  // open: lt
  Comparator #(.Bits(32)) GM_2 (.a(VirtualAddress), .b(32'h100003ff), .eq(GM_2_eq), .lt(GM_2_lt));  // open: gt
  Comparator #(.Bits(32)) Stack (.a(VirtualAddress), .b(32'h7fffebfc), .gt(Stack_gt), .eq(Stack_eq));  // open: lt
  Comparator #(.Bits(32)) Stack_2 (.a(VirtualAddress), .b(32'h7fffeffb), .eq(Stack_2_eq), .lt(Stack_2_lt));  // open: gt
  or or_1 (or_1_out, GM_gt, GM_eq);
  or or_2 (or_2_out, GM_2_eq, GM_2_lt);
  or or_3 (or_3_out, Stack_gt, Stack_eq);
  or or_4 (or_4_out, Stack_2_eq, Stack_2_lt);
  and and_1 (and_1_out, or_1_out, or_2_out);
  and and_2 (and_2_out, or_3_out, or_4_out);
  Multiplexer #(.Bits(32)) multiplexer_1 (
    .sel(and_1_out), .in_0({32{1'b0}}), .in_1(VirtualAddress), .out(multiplexer_1_out));
  Add #(.Bits(32)) add_1 (.a(VirtualAddress), .b(32'h4), .c_i(1'b0), .s(add_1_s));  // open: c_o
  not not_1 (not_1_out, and_2_out);
  not not_2 (not_2_out, and_1_out);
  and and_3 (and_3_out, not_1_out, not_2_out);
  Multiplexer #(.Bits(32)) multiplexer_2 (
    .sel(Enable), .in_0({32{1'b0}}), .in_1(multiplexer_1_out), .out(multiplexer_2_out));
  Multiplexer #(.Bits(32)) multiplexer_3 (.sel(and_2_out), .in_0({32{1'b0}}), .in_1(add_1_s), .out(multiplexer_3_out));
  Multiplexer #(.Bits(32)) multiplexer_4 (
    .sel(Enable), .in_0({32{1'b0}}), .in_1(multiplexer_3_out), .out(multiplexer_4_out));
  Multiplexer multiplexer_5 (.sel(and_3_out), .in_0(1'b0), .in_1(1'b1), .out(multiplexer_5_out));
  Multiplexer multiplexer_6 (.sel(Enable), .in_0(1'b0), .in_1(multiplexer_5_out), .out(InvalidAddress));
  assign {or_5_out, PhysicalAddress} = multiplexer_2_out | multiplexer_4_out;  // Or or_5, 32 bits wide

  // Other names for the same wires on the sheet: en = Enable; va[31:0] = VirtualAddress
endmodule

/* Test case:
Enable	VirtualAddress	PhysicalAddress	InvalidAddress
1	0x10000000	0		0
1	0x100003FF	1023		0
1	0x10000138	312		0
0	0x10000138	0		0
1	0x10873487	0		1
1	0x7FFFEBFC	1024		0
1	0x7FFFEFFB	2047		0
1	0x7FFFEEF9	1789		0
1	0x8FFFB45A	0		1
*/
