// Digital circuit ALUControl.dig as structural Verilog
module ALUControl (
  input  [3:0] aluOp,
  input  [5:0] Func,
  output [3:0] aluFunc,
  output mfhi,
  output mflo
);

  wire ADD_eq, AND_eq, comparator_1_eq, DIV_eq, LUI_eq, MFHI_eq, MFLO_eq, MULT_eq, OR_eq,
       priorityencoder_1_any, SLT_eq, SUB_eq, XOR_eq;
  wire [3:0] multiplexer_2_out, priorityencoder_1_num;

  Comparator #(.Bits(6)) AND (.a(Func), .b(6'b100100), .eq(AND_eq));  // open: gt, lt
  Comparator #(.Bits(6)) OR (.a(Func), .b(6'b100101), .eq(OR_eq));  // open: gt, lt
  Comparator #(.Bits(6)) ADD (.a(Func), .b(6'b100000), .eq(ADD_eq));  // open: gt, lt
  Comparator #(.Bits(6)) SUB (.a(Func), .b(6'b100010), .eq(SUB_eq));  // open: gt, lt
  Comparator #(.Bits(6)) SLT (.a(Func), .b(6'b101010), .eq(SLT_eq));  // open: gt, lt
  Comparator #(.Bits(6)) XOR (.a(Func), .b(6'b100110), .eq(XOR_eq));  // open: gt, lt
  Comparator #(.Bits(6)) LUI (.a(Func), .b(6'b001111), .eq(LUI_eq));  // open: gt, lt
  Comparator #(.Signed("true"), .Bits(6)) MULT (.a(Func), .b(6'b011000), .eq(MULT_eq));  // open: gt, lt
  Comparator #(.Signed("true"), .Bits(6)) DIV (.a(Func), .b(6'b011010), .eq(DIV_eq));  // open: gt, lt
  Comparator #(.Signed("true"), .Bits(6)) u_MFHI (.a(Func), .b(6'b010000), .eq(MFHI_eq));  // open: gt, lt
  Comparator #(.Signed("true"), .Bits(6)) u_MFLO (.a(Func), .b(6'b010010), .eq(MFLO_eq));  // open: gt, lt
  Comparator #(.Bits(4)) comparator_1 (.a(aluOp), .b(4'b1111), .eq(comparator_1_eq));  // open: gt, lt
  PriorityEncoder #(.Selector_Bits(4)) priorityencoder_1 (
    .in0(AND_eq), .in1(OR_eq), .in2(ADD_eq), .in3(SUB_eq), .in4(SLT_eq), .in5(XOR_eq), .in6(LUI_eq),
    .in7(MULT_eq), .in8(DIV_eq), .in9(MFHI_eq), .in10(MFLO_eq), .in11(1'b0), .in12(1'b0), .in13(1'b0),
    .in14(1'b0), .in15(1'b0), .num(priorityencoder_1_num), .any(priorityencoder_1_any));
  Multiplexer #(.Bits(4)) multiplexer_1 (.sel(comparator_1_eq), .in_0(aluOp), .in_1(multiplexer_2_out), .out(aluFunc));
  Multiplexer #(.Bits(4)) multiplexer_2 (
    .sel(priorityencoder_1_any), .in_0(4'b1111), .in_1(priorityencoder_1_num), .out(multiplexer_2_out));
  Comparator #(.Bits(4)) comparator_2 (.a(aluFunc), .b(4'b1001), .eq(mfhi));  // open: gt, lt
  Comparator #(.Bits(4)) comparator_3 (.a(aluFunc), .b(4'b1010), .eq(mflo));  // open: gt, lt
endmodule
