// Digital circuit MIPS32SOC.dig as structural Verilog
module MIPS32SOC (
  input  clk,
  input  rst,
  output invalid_opcode,
  output invalid_addr,
  output invalid_pc
);

  wire alu_1_iszero, aluSrc, and_1_out, and_2_out, beq, bne, jump, memRead, memToReg, memWrite, mfhi, mflo,
       not_1_out, or_1_out, or_2_out, RegDst, RegWrite, zeroExt;
  wire [1:0] priorityencoder_1_num;
  wire [3:0] add_1_s_2, aluFunc, aluOp;
  wire [4:0] multiplexer_2_out;
  wire [5:0] Func, Opcode;
  wire [9:0] pcdecoder_1_physicalpc;
  wire [10:0] memdecoder_1_physicaladdress;
  wire [25:6] InstMem_d;
  wire [27:0] add_1_s;
  wire [31:0] add_2_s, alu_1_res, bitextender_1_out, Data_Mem_d, hi, high, lo, low, multiplexer_1_out,
       multiplexer_3_out, multiplexer_4_out, multiplexer_5_out, multiplexer_6_out, multiplexer_7_out, PC_q,
       Reg_File_da, Reg_File_db, wData;

  Multiplexer #(.Bits(32)) multiplexer_1 (
    .sel(rst), .in_0(multiplexer_6_out), .in_1(32'h400000), .out(multiplexer_1_out));
  Register #(.Bits(32)) PC (.D(multiplexer_1_out), .C(clk), .en(1'b1), .Q(PC_q));
  PCDecoder pcdecoder_1 (.VirtualPC(PC_q), .PhysicalPC(pcdecoder_1_physicalpc), .InvalidPC(invalid_pc));
  Add #(.Bits(32)) add_1 (.a(PC_q), .b(32'h4), .c_i(1'b0), .s({add_1_s_2, add_1_s}));  // open: c_o
  ROM #(.AddrBits(8), .Bits(32)) InstMem (.A(pcdecoder_1_physicalpc[9:2]), .sel(1'b1), .D({Opcode, InstMem_d, Func}));
  ControlUnit controlunit_1 (
    .rst(rst), .Opcode(Opcode), .memWrite(memWrite), .memRead(memRead), .memToReg(memToReg), .aluOp(aluOp),
    .RegDst(RegDst), .aluSrc(aluSrc), .RegWrite(RegWrite), .beq(beq), .jump(jump), .bne(bne),
    .zeroExtend(zeroExt));
  Multiplexer #(.Bits(5)) multiplexer_2 (
    .sel(RegDst), .in_0(InstMem_d[20:16]), .in_1(InstMem_d[15:11]), .out(multiplexer_2_out));
  ALUControl alucontrol_1 (.aluOp(aluOp), .Func(Func), .aluFunc(aluFunc), .mfhi(mfhi), .mflo(mflo));
  BitExtender #(.inputBits(16), .outputBits(32)) bitextender_1 (.in({InstMem_d[15:6], Func}), .out(bitextender_1_out));
  RegisterFile #(.AddrBits(5), .Bits(32)) Reg_File (
    .Din(wData), .we(RegWrite), .Rw(multiplexer_2_out), .C(clk), .Ra(InstMem_d[25:21]),
    .Rb(InstMem_d[20:16]), .Da(Reg_File_da), .Db(Reg_File_db));
  Multiplexer #(.Bits(32)) multiplexer_3 (
    .sel(zeroExt), .in_0(bitextender_1_out), .in_1({{16{1'b0}}, InstMem_d[15:6], Func}),
    .out(multiplexer_3_out));
  Multiplexer #(.Bits(32)) multiplexer_4 (
    .sel(aluSrc), .in_0(Reg_File_db), .in_1(multiplexer_3_out), .out(multiplexer_4_out));
  and and_1 (and_1_out, beq, alu_1_iszero);
  Add #(.Bits(32)) add_2 (
    .a({add_1_s_2, add_1_s}), .b({bitextender_1_out[29:0], 2'b00}), .c_i(1'b0), .s(add_2_s));  // open: c_o
  not not_1 (not_1_out, alu_1_iszero);
  ALU alu_1 (
    .a(Reg_File_da), .b(multiplexer_4_out), .op(aluFunc), .clk(clk), .res(alu_1_res), .isZero(alu_1_iszero),
    .mult_high(hi), .div_low(lo));  // open: mult_low
  Register #(.Bits(32)) u_High (.D(hi), .C(clk), .en(RegWrite), .Q(high));
  Register #(.Bits(32)) u_Low (.D(lo), .C(clk), .en(RegWrite), .Q(low));
  Multiplexer #(.Bits(32)) multiplexer_5 (
    .sel(or_2_out), .in_0({add_1_s_2, add_1_s}), .in_1(add_2_s), .out(multiplexer_5_out));
  and and_2 (and_2_out, bne, not_1_out);
  Multiplexer #(.Bits(32)) multiplexer_6 (
    .sel(jump), .in_0(multiplexer_5_out), .in_1({add_1_s_2, InstMem_d, Func, 2'b00}), .out(multiplexer_6_out));
  or or_1 (or_1_out, memWrite, memRead);
  or or_2 (or_2_out, and_1_out, and_2_out);
  MemDecoder memdecoder_1 (
    .VirtualAddress(alu_1_res), .Enable(or_1_out), .PhysicalAddress(memdecoder_1_physicaladdress),
    .InvalidAddress(invalid_addr));
  RAMDualPort #(.AddrBits(8), .Bits(32)) Data_Mem (
    .A(memdecoder_1_physicaladdress[9:2]), .Din(Reg_File_db), .str(memWrite), .C(clk), .ld(memRead),
    .D(Data_Mem_d));
  Multiplexer #(.Bits(32)) multiplexer_7 (.sel(memToReg), .in_0(alu_1_res), .in_1(Data_Mem_d), .out(multiplexer_7_out));
  PriorityEncoder #(.Selector_Bits(2)) priorityencoder_1 (
    .in0(memToReg), .in1(mflo), .in2(mfhi), .in3(1'b0), .num(priorityencoder_1_num));  // open: any
  Multiplexer #(.Bits(32), .Selector_Bits(2)) multiplexer_8 (
    .sel(priorityencoder_1_num), .in_0(multiplexer_7_out), .in_1(low), .in_2(high), .in_3({32{1'b0}}),
    .out(wData));

  assign invalid_opcode = 1'b0;

  // Other names for the same wires on the sheet: invalidAddress = invalid_addr; invalidPC = invalid_pc

  // Notes on the sheet:
  //   contents of InstMem (hex, n*v repeats v):
  //   8c080000,8c090004,ac080008
endmodule
