// Digital circuit PCDecoder.dig as structural Verilog
module PCDecoder (
  input  [31:0] VirtualPC,
  output [9:0] PhysicalPC,
  output InvalidPC
);

  wire and_1_out, comparator_1_eq, comparator_1_gt, comparator_2_eq, comparator_2_lt, or_1_out, or_2_out;
  wire [31:10] multiplexer_1_out;

  Comparator #(.Bits(32)) comparator_1 (
    .a(VirtualPC), .b(32'h400000), .gt(comparator_1_gt), .eq(comparator_1_eq));  // open: lt
  Comparator #(.Bits(32)) comparator_2 (
    .a(VirtualPC), .b(32'h4003ff), .eq(comparator_2_eq), .lt(comparator_2_lt));  // open: gt
  or or_1 (or_1_out, comparator_1_gt, comparator_1_eq);
  or or_2 (or_2_out, comparator_2_eq, comparator_2_lt);
  and and_1 (and_1_out, or_1_out, or_2_out);
  Multiplexer #(.Bits(32)) multiplexer_1 (
    .sel(and_1_out), .in_0({32{1'b0}}), .in_1(VirtualPC), .out({multiplexer_1_out, PhysicalPC}));
  Multiplexer multiplexer_2 (.sel(and_1_out), .in_0(1'b1), .in_1(1'b0), .out(InvalidPC));
endmodule

/* Test case:
VirtualPC	PhysicalPC	InvalidPC
0x400000	0		0
0x4003FF	1023		0
0x400278	632		0
0x500534	0		1
0x500534	0		0
*/
